# Fritzing sketch arduino-3rfid (saved by Fritzing 0.9.3b)
breadboards: 1

parts:
  Part2 = RFID-RC522-v2
  Composant1 = Arduino Uno (Rev3)
  Part3 = RFID-RC522-v2
  Part4 = RFID-RC522-v2

nets:
  N1: Part2.SDA, Composant1.D2
  N2: Part2.SCK, Composant1.D13/SCK, Part3.SCK, Part4.SCK
  N3: Part2.MOSI, Composant1.D11_PWM/MOSI, Part3.MOSI, Part4.MOSI
  N4: Part2.MISO, Composant1.D12/MISO, Part3.MISO, Part4.MISO
  GND: Part2.GND, Composant1.GND, Part3.GND, Part4.GND
  N5: Part2.RST, Composant1.D9_PWM, Part3.RST, Part4.RST
  N6: Part2.3_3V, Composant1.3V3, Part3.3_3V, Part4.3_3V
  N7: Composant1.D3_PWM, Part3.SDA
  N8: Composant1.D4, Part4.SDA

notes:
  SDA/NSS
  SCK
  MOSI
  MISO
  GND
  RST
  3.3 V
  VCC
  D9
  D12
  D11
  D13
  D2, D3, D4

custom parts:
  RFID-RC522-v2: A simple China made RFID-RC522 Reader; do check the pin labels, as this is a MFRC522 based clone.
